# Fritzing sketch quiz (saved by Fritzing 0.9.6b)
breadboards: 3

parts:
  U1 = 74HC04_HEX_INVERTER [package=dil14]
  IC5 = SN74LS08N [package="DIP (Dual Inline) [THT]"]
  IC6 = SN74LS08N [package="DIP (Dual Inline) [THT]"]
  IC7 = SN74LS08N [package="DIP (Dual Inline) [THT]"]
  IC8 = SN74LS08N [package="DIP (Dual Inline) [THT]"]
  CD4044BE1 = CD4044BE [part_number=CD4044BE package="DIP (Dual Inline) [THT]"]
  CD4044BE2 = CD4044BE [part_number=CD4044BE package="DIP (Dual Inline) [THT]"]
  S1 = Momentary Switch [package=ksa_sealed_tac_switch]
  S2 = Momentary Switch [package=ksa_sealed_tac_switch]
  S3 = Momentary Switch [package=ksa_sealed_tac_switch]
  S4 = Momentary Switch [package=ksa_sealed_tac_switch]
  S5 = Momentary Switch [package=ksa_sealed_tac_switch]
  S6 = Momentary Switch [package=ksa_sealed_tac_switch]
  S7 = Momentary Switch [package=ksa_sealed_tac_switch]
  U2 = LuaNode32 / ESP32 [part_number=ESP32S-PIN30]

nets:
  N1: U1.1A, CD4044BE1.Q1, U2.D18
  N2: U1.1Y, IC6.1A
  N3: U1.2A, CD4044BE1.Q2, U2.TX2
  N4: U1.2Y, IC6.1B
  N5: U1.3A, CD4044BE1.Q3, U2.RX2
  N6: U1.3Y, IC6.2B
  GND: U1.GND, IC5.GND, IC6.GND, IC7.GND, IC8.GND, CD4044BE1.GND, CD4044BE2.GND, U2.GND
  N7: U1.4Y, IC5.1B
  N8: U1.4A, CD4044BE1.Q4, U2.D4
  N9: U1.5Y, IC5.2B
  N10: U1.5A, CD4044BE2.Q1, U2.D2
  N11: U1.6Y, IC5.3B
  N12: U1.6A, CD4044BE2.Q2, U2.D15
  VCC: U1.VCC, IC5.VCC, IC6.VCC, IC7.VCC, IC8.VCC, CD4044BE1.ENABLE, CD4044BE1.VCC, CD4044BE2.ENABLE, CD4044BE2.VCC, S1.4, S2.4, S3.4, S4.4, S5.4, S6.4, S7.4, U2.3V3
  N13: IC5.1A, IC6.2Y
  N14: IC5.1Y, IC5.2A
  N15: IC5.2Y, IC5.3A
  N16: IC5.3Y, IC7.1B, IC7.2B, IC7.3B, IC7.4B, IC8.1B, IC8.2B
  N17: IC6.1Y, IC6.2A
  N18: IC7.1A, S3.1
  N19: IC7.1Y, CD4044BE1.S3
  N20: IC7.2A, S4.1
  N21: IC7.2Y, CD4044BE1.S4
  N22: IC7.3Y, CD4044BE2.S2
  N23: IC7.3A, S6.1
  N24: IC7.4Y, CD4044BE2.S1
  N25: IC7.4A, S5.1
  N26: IC8.1A, S1.1
  N27: IC8.1Y, CD4044BE1.S1
  N28: IC8.2A, S2.1
  N29: IC8.2Y, CD4044BE1.S2

notes:
  Q1 |Yellow |18
  Q2 |Green |17
  Q3 |Orange |16
  Q4 |Purple |4
  Q5 |Red |2
  Q6 |Blue |15

custom parts:
  SN74LS08N: IC containing quadruple 2-input positive-AND gates.
  CD4044BE: A Dual 2 to 4 DEMX / Decoder
  LuaNode32 / ESP32: New Image for LuaNode32 DOIT ESP32 DEVKIT V1. Base parts from LuaNode32 / ESP32 ESP32 based LuaNode32 by G.Noorlander DOIT Esp32 DevKit v1 (30 pins long, 11 pins width) by Werner Rothschopf (modified by vanepp Dec 2018)
